// Logisim project SDMAC.circ as structural Verilog: 7 circuits, main circuit FIFO
module FIFO (
  input  INCNI,
  input  [31:0] ID,
  input  INCNO,
  input  INCBO,
  input  nRST,
  input  MID25,
  input  ACR_WR,
  input  h_0C,
  input  LHW,
  input  nLB,
  input  LLW,
  output [31:0] OD
);

  wire fifo_bytepointer_1_bo0, fifo_bytepointer_1_bo1, fifo_writestrobes_1_llws, fifo_writestrobes_1_lmws,
       fifo_writestrobes_1_umws, fifo_writestrobes_1_uuws;
  wire [7:0] ReadPointer_d, WritePointer_d;

  FIFO_BytePointer fifo_bytepointer_1 (
    .INCBO(INCBO), .nRST(nRST), .MID25(MID25), .ACR_WR(ACR_WR), .h_0C(h_0C), .BO0(fifo_bytepointer_1_bo0),
    .BO1(fifo_bytepointer_1_bo1));
  FIFO_NextLocationPointer WritePointer (.Inc(INCNI), .nRST(nRST), .D(WritePointer_d));
  FIFO_NextLocationPointer ReadPointer (.Inc(INCNO), .nRST(nRST), .D(ReadPointer_d));
  FIFO_WriteStrobes fifo_writestrobes_1 (
    .BO0(fifo_bytepointer_1_bo0), .BO1(fifo_bytepointer_1_bo1), .lhw(LHW), .nlb(nLB), .llw(LLW),
    .LLWS(fifo_writestrobes_1_llws), .LMWS(fifo_writestrobes_1_lmws), .UMWS(fifo_writestrobes_1_umws),
    .UUWS(fifo_writestrobes_1_uuws));
  FIFO_Buffer fifo_buffer_1 (
    .NI(WritePointer_d), .NO(ReadPointer_d), .DIN(ID), .LLWS(fifo_writestrobes_1_llws),
    .LMWS(fifo_writestrobes_1_lmws), .UMWS(fifo_writestrobes_1_umws), .UUWS(fifo_writestrobes_1_uuws),
    .DOUT(OD));
endmodule

module FIFO_WriteStrobes (
  input  BO0,
  input  BO1,
  input  lhw,
  input  nlb,
  input  llw,
  output LLWS,
  output LMWS,
  output UMWS,
  output UUWS
);

  wire nor_1_out, nor_2_out, nor_3_out, nor_4_out, nor_5_out, nor_6_out, nor_7_out, nor_8_out, not_1_out,
       not_2_out;

  not not_1 (not_1_out, BO0);
  not not_2 (not_2_out, BO1);
  nor nor_1 (nor_1_out, not_1_out, BO1, nlb);
  nor nor_2 (nor_2_out, not_2_out, BO0, nlb);
  nor nor_3 (nor_3_out, not_2_out, not_1_out, nlb);
  nor nor_4 (nor_4_out, BO0, BO1, nlb);
  nor nor_5 (nor_5_out, nor_4_out, lhw);
  not not_3 (UUWS, nor_5_out);
  nor nor_6 (nor_6_out, nor_1_out, lhw);
  not not_4 (UMWS, nor_6_out);
  nor nor_7 (nor_7_out, nor_2_out, llw);
  not not_5 (LMWS, nor_7_out);
  nor nor_8 (nor_8_out, nor_3_out, llw);
  not not_6 (LLWS, nor_8_out);
endmodule

module FIFO_BytePointer (
  input  INCBO,
  input  nRST,
  input  MID25,
  input  ACR_WR,
  input  h_0C,
  output BO0,
  output BO1
);

  wire d_ff_1_qn, multiplexer_1_out, not_1_out, not_2_out, not_3_out, not_4_out, or_1_out, xnor_1_out;

  not not_1 (not_1_out, nRST);
  xnor xnor_1 (xnor_1_out, BO1, BO0);
  not not_2 (not_2_out, MID25);
  or or_1 (or_1_out, INCBO, ACR_WR);
  not not_3 (not_3_out, d_ff_1_qn);
  Multiplexer multiplexer_1 (.in0(xnor_1_out), .in1(not_2_out), .out(multiplexer_1_out), .sel(h_0C));
  not not_4 (not_4_out, not_3_out);
  D_Flip_Flop d_ff_1 (.D(not_4_out), .clk(INCBO), .Q(BO0), .Qn(d_ff_1_qn), .reset(not_1_out));  // open: preset
  D_Flip_Flop d_ff_2 (.D(multiplexer_1_out), .clk(or_1_out), .Q(BO1));  // open: Qn, preset, reset

  // Notes on the sheet:
  //   nRST: initial=0x1
endmodule

module FIFO_NextLocationPointer (
  input  Inc,
  input  nRST,
  output [7:0] D
);

  wire d_ff_1_qn, d_ff_2_qn, nor_1_out, not_1_out, not_2_out, not_3_out, not_4_out, not_5_out, not_6_out,
       not_7_out, xor_1_out, xor_2_out;
  wire [2:0] d_ff_1_q;

  not not_1 (not_1_out, nRST);
  xor xor_1 (xor_1_out, d_ff_1_q[1], d_ff_1_q[0]);
  xor xor_2 (xor_2_out, d_ff_1_q[2], nor_1_out);
  not not_2 (not_2_out, d_ff_1_qn);
  not not_3 (not_3_out, not_4_out);
  not not_4 (not_4_out, xor_1_out);
  not not_5 (not_5_out, xor_2_out);
  not not_6 (not_6_out, not_5_out);
  D_Flip_Flop d_ff_1 (.D(not_7_out), .clk(Inc), .Q(d_ff_1_q[0]), .Qn(d_ff_1_qn), .reset(not_1_out));  // open: preset
  not not_7 (not_7_out, not_2_out);
  D_Flip_Flop d_ff_2 (.D(not_3_out), .clk(Inc), .Q(d_ff_1_q[1]), .Qn(d_ff_2_qn), .reset(not_1_out));  // open: preset
  D_Flip_Flop d_ff_3 (.D(not_6_out), .clk(Inc), .Q(d_ff_1_q[2]), .reset(not_1_out));  // open: Qn, preset
  nor nor_1 (nor_1_out, d_ff_2_qn, d_ff_1_qn);
  Decoder #(.enable("false"), .select(3)) decoder_1 (
    .out0(D[0]), .out1(D[1]), .out2(D[2]), .out3(D[3]), .out4(D[4]), .out5(D[5]), .out6(D[6]), .out7(D[7]),
    .sel(d_ff_1_q));
endmodule

module FIFO_Buffer (
  input  [7:0] NI,
  input  [7:0] NO,
  input  [31:0] DIN,
  input  LLWS,
  input  LMWS,
  input  UMWS,
  input  UUWS,
  output [31:0] DOUT
);

  FIFO_LongWordBuffer fifo_longwordbuffer_1 (
    .DIN(DIN), .LLWS(LLWS), .NI(NI[0]), .NO(NO[0]), .LMWS(LMWS), .UMWS(UMWS), .UUWS(UUWS), .DOUT(DOUT));
  FIFO_LongWordBuffer fifo_longwordbuffer_2 (
    .DIN(DIN), .LLWS(LLWS), .NI(NI[1]), .NO(NO[1]), .LMWS(LMWS), .UMWS(UMWS), .UUWS(UUWS), .DOUT(DOUT));
  FIFO_LongWordBuffer fifo_longwordbuffer_3 (
    .DIN(DIN), .LLWS(LLWS), .NI(NI[2]), .NO(NO[2]), .LMWS(LMWS), .UMWS(UMWS), .UUWS(UUWS), .DOUT(DOUT));
  FIFO_LongWordBuffer fifo_longwordbuffer_4 (
    .DIN(DIN), .LLWS(LLWS), .NI(NI[3]), .NO(NO[3]), .LMWS(LMWS), .UMWS(UMWS), .UUWS(UUWS), .DOUT(DOUT));
  FIFO_LongWordBuffer fifo_longwordbuffer_5 (
    .DIN(DIN), .LLWS(LLWS), .NI(NI[4]), .NO(NO[4]), .LMWS(LMWS), .UMWS(UMWS), .UUWS(UUWS), .DOUT(DOUT));
  FIFO_LongWordBuffer fifo_longwordbuffer_6 (
    .DIN(DIN), .LLWS(LLWS), .NI(NI[5]), .NO(NO[5]), .LMWS(LMWS), .UMWS(UMWS), .UUWS(UUWS), .DOUT(DOUT));
  FIFO_LongWordBuffer fifo_longwordbuffer_7 (
    .DIN(DIN), .LLWS(LLWS), .NI(NI[6]), .NO(NO[6]), .LMWS(LMWS), .UMWS(UMWS), .UUWS(UUWS), .DOUT(DOUT));
  FIFO_LongWordBuffer fifo_longwordbuffer_8 (
    .DIN(DIN), .LLWS(LLWS), .NI(NI[7]), .NO(NO[7]), .LMWS(LMWS), .UMWS(UMWS), .DOUT(DOUT));  // open: UUWS
endmodule

module FIFO_LongWordBuffer (
  input  [31:0] DIN,
  input  LLWS,
  input  NI,
  input  NO,
  input  LMWS,
  input  UMWS,
  input  UUWS,
  output [31:0] DOUT
);

  wire buffer_1_out, nand_1_out, nand_2_out, nand_3_out, nand_4_out, not_1_out, not_2_out, not_3_out,
       not_4_out;
  wire [7:0] register_1_q, register_2_q, register_3_q, register_4_q;

  nand nand_1 (nand_1_out, LLWS, NI);
  buf buffer_1 (buffer_1_out, NO);
  nand nand_2 (nand_2_out, LMWS, NI);
  nand nand_3 (nand_3_out, UMWS, NI);
  nand nand_4 (nand_4_out, UUWS, NI);
  not not_1 (not_1_out, nand_1_out);
  not not_2 (not_2_out, nand_2_out);
  not not_3 (not_3_out, nand_3_out);
  not not_4 (not_4_out, nand_4_out);
  Register register_1 (.D(DIN[7:0]), .en(not_1_out), .clk(not_1_out), .Q(register_1_q), .clr(1'b0));
  Register register_2 (.D(DIN[15:8]), .en(not_2_out), .clk(not_2_out), .Q(register_2_q), .clr(1'b0));
  Register register_3 (.D(DIN[23:16]), .en(not_3_out), .clk(not_3_out), .Q(register_3_q), .clr(1'b0));
  Register register_4 (.D(DIN[31:24]), .en(not_4_out), .clk(not_4_out), .Q(register_4_q), .clr(1'b0));
  assign DOUT[7:0] = buffer_1_out ? register_1_q : 8'bz;  // Controlled_Buffer controlled_buffer_1
  assign DOUT[15:8] = buffer_1_out ? register_2_q : 8'bz;  // Controlled_Buffer controlled_buffer_2
  assign DOUT[23:16] = buffer_1_out ? register_3_q : 8'bz;  // Controlled_Buffer controlled_buffer_3
  assign DOUT[31:24] = buffer_1_out ? register_4_q : 8'bz;  // Controlled_Buffer controlled_buffer_4

  // Notes on the sheet:
  //   DIN: initial=0xaaaaaa
endmodule

module SDMAC_MAIN (
);

  FIFO fifo_1 ();  // open: INCNI, ID, INCNO, INCBO, nRST, MID25, ACR_WR, h_0C, LHW, nLB, LLW, OD
endmodule
